# Fritzing sketch Avionic-Ground (saved by Fritzing 0.9.3b)

parts:
  Part1 = Arduino Uno (Rev3) - ICSP
  Part2 = Arduino Nano (Rev3.0)
  Part3 = InvenSense MPU6050
  Part6 = NRF24L01
  J1 = Piezo Speaker
  Part5 = BME280 Breakout
  Part7 = NRF24L01
  J2 = Dagu DGServo 9g header connector (female) [package=THT]
  Q1 = NPN-Transistor [package="TO92 [THT]"]
  microSD1 = MicroSD Card Module
  L1 = Inductor [package="400 mil [THT]"]  # not connected
  VCC1 = Battery block 9V  # not connected
  M1 = Dagu DGServo 9g (End View) [part_number=RS001B]
  S1 = Round Pushbutton

nets:
  N1: Part1.A0, J2.Vcc, Q1.C
  N2: Part1.A4/SDA, Part3.SDA, Part5.SDI/SDA
  N3: Part1.A5/SCL, Part3.SCL, Part5.SCK/SCL
  N4: Part1.ICSP_MISO, Part1.D12/MISO, microSD1.MISO
  N5: Part1.D8, J1.pin2
  N6: Part1.D9_PWM, Part6.SCK
  N7: Part1.D10_PWM/SS, microSD1.SCK
  N8: Part1.D11_PWM/MOSI, microSD1.MOSI
  GND: Part1.GND, Part3.GND, Part6.GND, J1.pin1, Part5.GND, microSD1.GND, M1.gnd
  N9: Part1.D2, Part6.CSN
  N10: Part1.D3_PWM, Part6.CE
  N11: Part1.D4, microSD1.CS
  N12: Part1.D5_PWM, Part6.MOSI
  N13: Part1.D6_PWM, M1.pulse
  N14: Part1.D7, Part6.MISO
  VCC: Part1.5V, Part3.VCC, Part6.VCC, Part5.3.3V, microSD1.VCC, M1.vcc
  GND_2: Part2.GND, Part7.GND, S1.leg1
  N15: Part2.D2, Part7.CSN
  N16: Part2.D3, Part7.CE
  N17: Part2.D4, S1.leg0
  N18: Part2.D5, Part7.MOSI
  N19: Part2.D7, Part7.IRQ
  N20: Part2.D9, Part7.SCK
  5V: Part2.5V, Part7.VCC
